// Logisim project projetoCirc.circ as structural Verilog: 9 circuits, main circuit [6] memoriaPalpite
module MAIN__circuitoCore (
  input  in_1,
  input  in_2,
  input  in_3,
  input  in_4,
  input  in_5,
  input  Palpite_do,
  input  in_7,
  input  in_8,
  input  Turnout,
  input  Reset,
  output Chutando_X,
  output Chutando_Y,
  output Resultado,
  output Maior,
  output Igual,
  output Menor,
  output Acertou
);

  wire _5_clockx, _5_clocky, _8_2_n, _8_n, and_1_out, and_2_out, button_1_out;
  wire [3:0] _1_2_out_2, _1_out_2, _6_2_out_4, _6_out_4, _8_2_out_3, _8_out_3, multiplexer_1_out;

  Button button_1 (.out(button_1_out));
  Multiplexer #(.width(4)) multiplexer_1 (
    .in0({in_1, in_2, in_3, in_4}), .in1({in_5, Palpite_do, in_7, in_8}), .out(multiplexer_1_out),
    .sel(Turnout));  // open: en
  _5__LEDS _5 (
    .in_1(button_1_out), .x(Chutando_X), .y(Chutando_Y), .c(Resultado), .clockX(_5_clockx), .clockY(_5_clocky));
  _6__memoriaPalpite _6 (.in_1(_5_clockx), .in_2(multiplexer_1_out), .reset(Reset), .out_4(_6_out_4));
  _8__visualizadorPalpites _8 (.e3(_6_out_4), .n(_8_n), .out_3(_8_out_3));
  _6__memoriaPalpite _6_2 (.in_1(_5_clocky), .in_2(multiplexer_1_out), .reset(Reset), .out_4(_6_2_out_4));
  _8__visualizadorPalpites _8_2 (.e3(_6_2_out_4), .n(_8_2_n), .out_3(_8_2_out_3));
  _7_Segment_Display u_7_segment_display_1 (.g(_8_n));  // open: f, a, b, e, d, c, dp
  Hex_Digit_Display hex_digit_display_1 (.value(_8_out_3));  // open: dp
  _7_Segment_Display u_7_segment_display_2 (.g(_8_2_n));  // open: f, a, b, e, d, c, dp
  Hex_Digit_Display hex_digit_display_2 (.value(_8_2_out_3));  // open: dp
  _7__somador _7 (
    .palpite_Coord__x(_6_out_4), .palpite_Coord__Y(_6_2_out_4), .in_1(Resultado), .maior(Maior),
    .igual__soma(Igual), .menor(Menor), .igual__coordenadas(Acertou));
  and and_1 (and_1_out, Acertou, ~Turnout);  // AND_Gate
  and and_2 (and_2_out, Acertou, Turnout);
  Hex_Digit_Display hex_digit_display_3 (.value(_1_out_2));  // open: dp
  _1__Pontuador _1 (.in_1(and_1_out), .out_2(_1_out_2));
  Hex_Digit_Display hex_digit_display_4 (.value(_1_2_out_2));  // open: dp
  _1__Pontuador _1_2 (.in_1(and_2_out), .out_2(_1_2_out_2));

  // Notes on the sheet:
  //   Palpite do
  //   jogador 0
  //   jogador 1
  //   Mudar estado
  //   Coord. X
  //   Coord. Y
  //   Pontuação do 
  //   jogador 0
  //   Pontuação do 
  //   jogador 1
endmodule

module _1__Pontuador (
  input  in_1,
  output [3:0] out_2
);

  wire n2_transicaopontuador_1_s0, n2_transicaopontuador_1_s1, n2_transicaopontuador_1_s2,
       n2_transicaopontuador_1_s3;

  D_Flip_Flop d_ff_1 (.clk(in_1), .D(n2_transicaopontuador_1_s3), .Q(out_2[3]));  // open: Qn, preset, en, reset
  D_Flip_Flop d_ff_2 (.clk(in_1), .D(n2_transicaopontuador_1_s2), .Q(out_2[2]));  // open: Qn, preset, en, reset
  D_Flip_Flop d_ff_3 (.clk(in_1), .D(n2_transicaopontuador_1_s1), .Q(out_2[1]));  // open: Qn, preset, en, reset
  _2__transicaoPontuador u_2_transicaopontuador_1 (
    .e0(out_2[3]), .e1(out_2[2]), .e2(out_2[1]), .e3(out_2[0]), .x(1'b1), .s3(n2_transicaopontuador_1_s3),
    .s2(n2_transicaopontuador_1_s2), .s1(n2_transicaopontuador_1_s1), .s0(n2_transicaopontuador_1_s0));
  D_Flip_Flop d_ff_4 (.clk(in_1), .D(n2_transicaopontuador_1_s0), .Q(out_2[0]));  // open: Qn, preset, en, reset
endmodule

// [2]
module _2__transicaoPontuador (
  input  e0,
  input  e1,
  input  e2,
  input  e3,
  input  x,
  output s3,
  output s2,
  output s1,
  output s0
);

  wire and_1_out, and_2_out, and_3_out, and_4_out, and_5_out, and_6_out, and_7_out, and_8_out, and_9_out,
       and_10_out, and_11_out, and_12_out, and_13_out, and_14_out, not_1_out, not_2_out, not_3_out,
       not_4_out, not_5_out, not_6_out, not_7_out, not_8_out, not_9_out, not_10_out, not_11_out, not_12_out,
       not_13_out, not_14_out;

  not not_1 (not_1_out, e0);
  not not_2 (not_2_out, e1);
  not not_3 (not_3_out, e2);
  not not_4 (not_4_out, e3);
  not not_5 (not_5_out, x);
  not not_6 (not_6_out, e1);
  not not_7 (not_7_out, e2);
  not not_8 (not_8_out, e3);
  not not_9 (not_9_out, x);
  not not_10 (not_10_out, e2);
  not not_11 (not_11_out, e3);
  not not_12 (not_12_out, x);
  not not_13 (not_13_out, e3);
  not not_14 (not_14_out, x);
  and and_1 (and_1_out, not_1_out, e1, e2, e3, x);
  and and_2 (and_2_out, e0, not_2_out);
  and and_3 (and_3_out, e0, not_3_out);
  and and_4 (and_4_out, e0, not_4_out);
  and and_5 (and_5_out, e0, not_5_out);
  and and_6 (and_6_out, not_6_out, e2, e3, x);
  and and_7 (and_7_out, e1, not_7_out);
  and and_8 (and_8_out, e1, not_8_out);
  and and_9 (and_9_out, e1, not_9_out);
  and and_10 (and_10_out, not_10_out, e3, x);
  and and_11 (and_11_out, e2, not_11_out);
  and and_12 (and_12_out, e2, not_12_out);
  and and_13 (and_13_out, not_13_out, x);
  and and_14 (and_14_out, e3, not_14_out);
  or or_1 (s3, and_1_out, and_2_out, and_3_out, and_4_out, and_5_out);
  or or_2 (s2, and_6_out, and_7_out, and_8_out, and_9_out);
  or or_3 (s1, and_10_out, and_11_out, and_12_out);
  or or_4 (s0, and_13_out, and_14_out);
endmodule

module _3__logicaLEDS (
  input  in_1,
  input  in_2,
  output out_3,
  output out_4,
  output out_5
);

  and and_1 (out_3, ~in_1, ~in_2);  // AND_Gate
  and and_2 (out_4, ~in_1, in_2);  // AND_Gate
  and and_3 (out_5, in_1, ~in_2);  // AND_Gate
endmodule

module _4__transicaoLEDS (
  input  e1,
  input  e0,
  output s1,
  output s0
);

  wire not_1_out, not_2_out;

  not not_1 (not_1_out, e1);
  not not_2 (not_2_out, e0);
  and and_1 (s0, not_1_out, not_2_out);

  assign s1 = e0;
endmodule

module _5__LEDS (
  input  in_1,
  output x,
  output y,
  output c,
  output clockX,
  output clockY
);

  wire _4_s0, _4_s1, d_ff_1_q, d_ff_2_q, not_1_out, not_2_out, not_3_out, not_4_out, not_5_out, not_6_out;

  _3__logicaLEDS _3 (.in_1(d_ff_1_q), .in_2(d_ff_2_q), .out_3(x), .out_4(y), .out_5(c));
  D_Flip_Flop d_ff_1 (.clk(in_1), .D(_4_s1), .Q(d_ff_1_q));  // open: Qn, preset, en, reset
  _4__transicaoLEDS _4 (.e1(d_ff_1_q), .e0(d_ff_2_q), .s1(_4_s1), .s0(_4_s0));
  D_Flip_Flop d_ff_2 (.clk(in_1), .D(_4_s0), .Q(d_ff_2_q));  // open: Qn, preset, en, reset
  not not_1 (not_1_out, y);
  not not_2 (not_2_out, c);
  not not_3 (not_3_out, not_1_out);
  not not_4 (not_4_out, not_3_out);
  not not_5 (not_5_out, not_6_out);
  not not_6 (not_6_out, not_2_out);
  not not_7 (clockX, not_4_out);
  not not_8 (clockY, not_5_out);
endmodule

module _6__memoriaPalpite (
  input  in_1,
  input  [3:0] in_2,
  input  reset,
  output [3:0] out_4
);

  D_Flip_Flop d_ff_1 (.clk(in_1), .D(in_2[0]), .Q(out_4[0]), .reset(reset));  // open: Qn, preset, en
  D_Flip_Flop d_ff_2 (.clk(in_1), .D(in_2[1]), .Q(out_4[1]), .reset(reset));  // open: Qn, preset, en
  D_Flip_Flop d_ff_3 (.clk(in_1), .D(in_2[2]), .Q(out_4[2]), .reset(reset));  // open: Qn, preset, en
  D_Flip_Flop d_ff_4 (.clk(in_1), .D(in_2[3]), .Q(out_4[3]), .reset(reset));  // open: Qn, preset, en
endmodule

module _7__somador (
  input  in_1,
  input  [3:0] palpite_Coord__x,
  input  [3:0] palpite_Coord__Y,
  output maior,
  output igual__soma,
  output menor,
  output igual__coordenadas
);

  wire and_1_out, button_1_out, comparator_1_eq, comparator_2_eq, comparator_3_eq, comparator_3_gt,
       comparator_3_lt;
  wire [3:0] bit_extender_5_out, bit_extender_6_out, Coord__X_out, Coord__Y_out;
  wire [4:0] adder_1_out, adder_2_out, bit_extender_1_out, bit_extender_2_out, bit_extender_3_out,
       bit_extender_4_out;

  Button button_1 (.out(button_1_out));
  Random #(.width(4), .seed(4)) Coord__X (.clk(button_1_out), .out(Coord__X_out));  // open: next, clr
  Random #(.width(4)) Coord__Y (.clk(button_1_out), .out(Coord__Y_out));  // open: next, clr
  assign bit_extender_1_out = {{1{1'b0}}, palpite_Coord__x};  // Bit_Extender bit_extender_1
  assign bit_extender_2_out = {{1{1'b0}}, palpite_Coord__Y};  // Bit_Extender bit_extender_2
  assign bit_extender_3_out = {{1{1'b0}}, Coord__X_out};  // Bit_Extender bit_extender_3
  assign bit_extender_4_out = {{1{1'b0}}, Coord__Y_out};  // Bit_Extender bit_extender_4
  Adder #(.width(5)) adder_1 (.a(bit_extender_1_out), .b(bit_extender_2_out), .out(adder_1_out));  // open: cin, cout
  Adder #(.width(5)) adder_2 (.a(bit_extender_3_out), .b(bit_extender_4_out), .out(adder_2_out));  // open: cin, cout
  Comparator #(.width(5)) comparator_1 (
    .a(bit_extender_1_out), .b(bit_extender_3_out), .eq(comparator_1_eq));  // open: gt, lt
  Comparator #(.width(5)) comparator_2 (
    .a(bit_extender_2_out), .b(bit_extender_4_out), .eq(comparator_2_eq));  // open: gt, lt
  Bit_Extender #(.in_width(5), .out_width(4)) bit_extender_5 (.in(adder_1_out), .out(bit_extender_5_out));
  Bit_Extender #(.in_width(5), .out_width(4)) bit_extender_6 (.in(adder_2_out), .out(bit_extender_6_out));
  Comparator #(.width(4)) comparator_3 (
    .a(bit_extender_5_out), .b(bit_extender_6_out), .gt(comparator_3_gt), .eq(comparator_3_eq),
    .lt(comparator_3_lt));
  and and_1 (and_1_out, comparator_1_eq, comparator_2_eq);
  and and_2 (maior, comparator_3_gt, in_1);
  and and_3 (igual__soma, comparator_3_eq, in_1);
  and and_4 (menor, comparator_3_lt, in_1);
  and and_5 (igual__coordenadas, in_1, and_1_out);

  // Notes on the sheet:
  //   //ver problema com geração dos aleatórios 
  //   soma palpites
  //   soma Coord.
endmodule

module _8__visualizadorPalpites (
  input  [3:0] e3,
  output n,
  output [3:0] out_3
);

  wire and_2_out, and_3_out, and_4_out, and_5_out, and_6_out, and_7_out, and_8_out, not_1_out, not_2_out,
       not_3_out, not_4_out, not_5_out, not_6_out, not_7_out, not_8_out, not_9_out, not_10_out, not_11_out;

  not not_1 (not_1_out, e3[2]);
  not not_2 (not_2_out, e3[1]);
  not not_3 (not_3_out, e3[0]);
  not not_4 (not_4_out, e3[3]);
  not not_5 (not_5_out, e3[1]);
  not not_6 (not_6_out, e3[0]);
  not not_7 (not_7_out, e3[2]);
  not not_8 (not_8_out, e3[2]);
  not not_9 (not_9_out, e3[3]);
  not not_10 (not_10_out, e3[0]);
  not not_11 (not_11_out, e3[1]);
  and and_1 (out_3[3], e3[3], not_1_out, not_2_out, not_3_out);
  and and_2 (and_2_out, not_4_out, e3[2]);
  and and_3 (and_3_out, e3[2], not_5_out, not_6_out);
  and and_4 (and_4_out, e3[3], not_7_out, e3[0]);
  and and_5 (and_5_out, e3[3], not_8_out, e3[1]);
  and and_6 (and_6_out, not_9_out, e3[1]);
  and and_7 (and_7_out, e3[1], not_10_out);
  and and_8 (and_8_out, e3[3], not_11_out, e3[0]);
  or or_1 (out_3[2], and_2_out, and_3_out, and_4_out, and_5_out);
  or or_2 (out_3[1], and_6_out, and_7_out, and_8_out);

  assign n = e3[3];
  assign out_3[0] = e3[0];
endmodule
